# Fritzing sketch Gotham-dino (saved by Fritzing 0.9.3b)
breadboards: 1

parts:
  LED1 = LED - 5mm [color="Red (633nm)" package="5 mm [THT]"]
  LED2 = LED - 5mm [color="Yellow (585nm)" package="5 mm [THT]"]
  LED3 = LED - 5mm [color="Green (565nm)" package="5 mm [THT]"]
  LED4 = LED - 5mm [color="Blue (470nm)" package="5 mm [THT]"]
  LED5 = LED - 5mm [color="White (4500K)" package="5 mm [THT]"]
  LED6 = LED - 5mm [color="Red (633nm)" package="5 mm [THT]"]
  R1 = Resistor [tolerance=±5% resistance=10 package=THT]
  R2 = Resistor [tolerance=±5% resistance=10 package=THT]
  R3 = Resistor [tolerance=±5% resistance=10 package=THT]
  R4 = Resistor [tolerance=±5% resistance=10 package=THT]
  R5 = Resistor [tolerance=±5% resistance=10 package=THT]
  R6 = Resistor [tolerance=±5% resistance=10 package=THT]
  Componente1 = Arduino Uno (Rev3)

nets:
  N1: LED1.cathode, R1.Pin_1
  N2: LED1.anode, LED2.anode, LED3.anode, LED4.anode, LED5.anode, LED6.anode, Componente1.GND
  N3: LED2.cathode, R2.Pin_1
  N4: LED3.cathode, R3.Pin_1
  N5: LED4.cathode, R4.Pin_1
  N6: LED5.cathode, R5.Pin_1
  N7: LED6.cathode, R6.Pin_1
  N8: R1.Pin_0, Componente1.D8
  N9: R2.Pin_0, Componente1.D9_PWM
  N10: R3.Pin_0, Componente1.D10_PWM/SS
  N11: R4.Pin_0, Componente1.D11_PWM/MOSI
  N12: R5.Pin_0, Componente1.D12/MISO
  N13: R6.Pin_0, Componente1.D13/SCK
