# Fritzing sketch Sensor Aparcamiento (saved by Fritzing 0.9.3b)
breadboards: 1

parts:
  Componente1 = Arduino Uno (Rev3)
  hc-sr1 = hc-sr04
  J1 = Piezo Speaker
  R1 = Resistor [tolerance=±5% resistance=100 package="2010 [SMD]"]

nets:
  N1: Componente1.D2, J1.pin2
  N2: Componente1.D3_PWM, hc-sr1.Trig
  N3: Componente1.D4, hc-sr1.Echo
  5V: Componente1.5V, hc-sr1.VCC
  GND: Componente1.GND, hc-sr1.GND, R1.Pin_0
  N4: J1.pin1, R1.Pin_1
